# Fritzing sketch chenillard (saved by Fritzing 0.9.3b)
circuit board: 8.50911cm x 5.60907cm
breadboards: 1

parts:
  Composant1 = Arduino Uno (Rev3)
  LED1 = LED - 5mm [color="Green (565nm)" package="5 mm [THT]"]
  LED2 = LED - 5mm [color="Orange (620nm)" package="5 mm [THT]"]
  LED3 = LED - 5mm [color="Red (633nm)" package="5 mm [THT]"]
  S1 = Pushbutton [package="[THT]"]
  R1 = Trimmer Potentiometer [maximum_resistance=10kΩ package=THT]
  R2 = Resistor [tolerance=±5% resistance=220 package=THT]

nets:
  N1: Composant1.A5/SCL, R1.wiper
  N2: Composant1.GND, LED1.cathode, LED2.cathode, LED3.cathode, R1.leg1, R2.Pin_1
  N3: Composant1.D2, S1.Pin_1, S1.Pin_2, R2.Pin_0
  N4: Composant1.D4, LED1.anode
  N5: Composant1.D5_PWM, LED2.anode
  N6: Composant1.D6_PWM, LED3.anode
  N7: Composant1.5V, S1.Pin_3, S1.Pin_4, R1.leg2
